# Fritzing sketch dht11_lcd16x2 (saved by Fritzing 0.9.3b)
breadboards: 1

parts:
  LCD1 = LCD screen
  Part1 = Arduino Uno (Rev3)
  R1 = TRIMPOT [package=trimpot_pth_s3_lock]
  RHT1 = Humidity and Temperature Sensor RHT03
  R2 = Resistor [tolerance=±5% resistance=10k package=THT]

nets:
  VSS: LCD1.VSS, LCD1.R/W, LCD1.LED-, Part1.GND, R1.CCW, R1.CW, RHT1.GND_2
  VDD: LCD1.VDD, LCD1.LED+, Part1.5V, RHT1.Vcc, R2.Pin_0
  N1: LCD1.V0, R1.WIPER
  N2: LCD1.RS, Part1.D12/MISO
  N3: LCD1.E, Part1.D11_PWM/MOSI
  N4: LCD1.DB4, Part1.D5_PWM
  N5: LCD1.DB5, Part1.D4
  N6: LCD1.DB6, Part1.D3_PWM
  N7: LCD1.DB7, Part1.D2
  N8: Part1.A1, RHT1.Data-signal, R2.Pin_1

notes:
  Trimpot:
  10k ohm
  Sensor:
  DHT11
