# Fritzing sketch display7seg-01 (saved by Fritzing 0.9.3b)
breadboards: 1

parts:
  Part1 = Arduino Uno (Rev3)
  U3 = 7-SEGMENT-DISPLAY [package=7-segment-display]
  R1 = Resistor [tolerance=±20% resistance=1k package=THT]
  R2 = Resistor [tolerance=±20% resistance=1k package=THT]
  R3 = Resistor [tolerance=±20% resistance=1k package=THT]
  R4 = Resistor [tolerance=±20% resistance=1k package=THT]
  R5 = Resistor [tolerance=±20% resistance=1k package=THT]
  R6 = Resistor [tolerance=±20% resistance=1k package=THT]
  R7 = Resistor [tolerance=±20% resistance=1k package=THT]
  R8 = Resistor [tolerance=±20% resistance=1k package=THT]

nets:
  N1: Part1.D8, R6.Pin_1
  N2: Part1.D9_PWM, R7.Pin_1
  N3: Part1.D10_PWM/SS, R8.Pin_1
  N4: Part1.D2, U3.C
  N5: Part1.D3_PWM, R1.Pin_1
  N6: Part1.D4, R2.Pin_1
  N7: Part1.D5_PWM, R3.Pin_1
  N8: Part1.D6_PWM, R4.Pin_1
  N9: Part1.D7, R5.Pin_1
  N10: U3.E, R7.Pin_0
  N11: U3.D, R5.Pin_0
  N12: U3.G1, R4.Pin_0
  N13: U3.DP, R3.Pin_0
  N14: U3.B, R8.Pin_0
  N15: U3.A, R2.Pin_0
  N16: U3.G2, R1.Pin_0
  N17: U3.G, R6.Pin_0
