# Fritzing sketch robot_speak01 (saved by Fritzing 0.9.2b)
breadboards: 1

parts:
  Part1 = Arduino Uno (Rev3)
  J1 = Piezo Speaker
  S1 = Pushbutton [package="[THT]"]
  LED1 = LED - 5mm [color="Red (633nm)" package="5 mm [THT]"]
  LED2 = LED - 5mm [color="Red (633nm)" package="5 mm [THT]"]
  R1 = Resistor [tolerance=±2% resistance=10k package=THT]
  R2 = Resistor [tolerance=±2% resistance=330 package=THT]
  R3 = Resistor [tolerance=±2% resistance=330 package=THT]
  LED3 = LED - 5mm [color="Green (555nm)" package="5 mm [THT]"]
  LED4 = LED - 5mm [color="Green (555nm)" package="5 mm [THT]"]
  LED5 = LED - 5mm [color="Green (555nm)" package="5 mm [THT]"]
  R4 = Resistor [tolerance=±2% resistance=330 package=THT]
  R5 = Resistor [tolerance=±2% resistance=330 package=THT]
  R6 = Resistor [tolerance=±2% resistance=330 package=THT]

nets:
  N1: Part1.D10_PWM/SS, J1.pin2
  N2: Part1.D2, S1.Pin_1, S1.Pin_2, R1.Pin_0
  N3: Part1.D3_PWM, R3.Pin_1
  N4: Part1.D4, R2.Pin_1
  N5: Part1.D5_PWM, R6.Pin_0
  N6: Part1.D6_PWM, R5.Pin_0
  N7: Part1.D7, R4.Pin_0
  N8: Part1.5V, S1.Pin_3, S1.Pin_4
  N9: Part1.GND, J1.pin1, LED1.cathode, LED2.cathode, R1.Pin_1, LED3.cathode, LED4.cathode, LED5.cathode
  N10: LED1.anode, R3.Pin_0
  N11: LED2.anode, R2.Pin_0
  N12: LED3.anode, R4.Pin_1
  N13: LED4.anode, R5.Pin_1
  N14: LED5.anode, R6.Pin_1
